// Logisim project Lab1_computadores.circ as structural Verilog: 6 circuits, main circuit main
module main (
  input  in_1,
  input  in_2,
  input  in_3,
  output out_4,
  output out_5
);

  Sumador sumador_1 (.A(in_2), .B(in_3), .Cin(in_1), .S(out_4), .Cout(out_5));
  Sumador_overflow sumador_overflow_1 ();  // open: A, B, Cin, S, Cout, Overflow
endmodule

module Sumador (
  input  A,
  input  B,
  input  Cin,
  output S,
  output Cout
);

  wire and_1_out, and_2_out, and_3_out, and_4_out, and_5_out, and_6_out, and_7_out, not_1_out, not_2_out,
       not_3_out, not_4_out, not_5_out, not_6_out;

  not not_1 (not_1_out, A);
  not not_2 (not_2_out, B);
  not not_3 (not_3_out, A);
  not not_4 (not_4_out, Cin);
  not not_5 (not_5_out, B);
  not not_6 (not_6_out, Cin);
  and and_1 (and_1_out, B, Cin);
  and and_2 (and_2_out, A, Cin);
  and and_3 (and_3_out, A, B);
  and and_4 (and_4_out, not_1_out, not_2_out, Cin);
  and and_5 (and_5_out, not_3_out, B, not_4_out);
  and and_6 (and_6_out, A, not_5_out, not_6_out);
  and and_7 (and_7_out, A, B, Cin);
  or or_1 (Cout, and_1_out, and_2_out, and_3_out);
  or or_2 (S, and_4_out, and_5_out, and_6_out, and_7_out);
endmodule

module Sumador_overflow (
  input  A,
  input  B,
  input  Cin,
  output S,
  output Cout,
  output Overflow
);

  wire and_1_out, and_2_out, and_3_out, and_4_out, and_5_out, and_6_out, and_7_out, and_8_out, and_9_out,
       not_1_out, not_2_out, not_3_out, not_4_out, not_5_out, not_6_out, not_7_out;

  not not_1 (not_1_out, A);
  not not_2 (not_2_out, B);
  not not_3 (not_3_out, A);
  not not_4 (not_4_out, Cin);
  not not_5 (not_5_out, B);
  not not_6 (not_6_out, Cin);
  and and_1 (and_1_out, B, Cin);
  and and_2 (and_2_out, A, Cin);
  and and_3 (and_3_out, A, B);
  and and_4 (and_4_out, not_1_out, not_2_out, Cin);
  and and_5 (and_5_out, not_3_out, B, not_4_out);
  and and_6 (and_6_out, A, not_5_out, not_6_out);
  and and_7 (and_7_out, A, B, Cin);
  or or_1 (Cout, and_1_out, and_2_out, and_3_out);
  not not_7 (not_7_out, Cout);
  or or_2 (S, and_4_out, and_5_out, and_6_out, and_7_out);
  and and_8 (and_8_out, not_7_out, Cin);
  and and_9 (and_9_out, not_6_out, Cout);
  or or_3 (Overflow, and_8_out, and_9_out);
endmodule

module ALU_bit_1 (
  input  A,
  input  B,
  input  Cint,
  input  [2:0] Op,
  output R,
  output Cout
);

  wire and_1_out, multiplexer_1_out, not_1_out, not_2_out, or_1_out, or_2_out, sumador_1_s, sumador_2_s;

  or or_1 (or_1_out, B, B);
  not not_1 (not_1_out, or_1_out);
  // Probe on or_1_out
  // Probe on not_1_out
  Sumador sumador_1 (.A(1'b1), .B(not_1_out), .Cin(1'b0), .S(sumador_1_s));  // open: Cout
  // Probe on sumador_1_s
  Multiplexer #(.select(3), .enable("false")) multiplexer_1 (
    .in0(B), .in1(sumador_1_s), .in2(B), .in3(B), .in4(B), .in5(B), .in6(B), .in7(B),
    .out(multiplexer_1_out), .sel(Op));
  and and_1 (and_1_out, B, A);
  or or_2 (or_2_out, B, A);
  not not_2 (not_2_out, or_2_out);
  Sumador sumador_2 (.A(A), .B(multiplexer_1_out), .Cin(Cint), .S(sumador_2_s), .Cout(Cout));
  // Probe on multiplexer_1_out
  Multiplexer #(.select(3), .enable("false")) multiplexer_2 (
    .in0(and_1_out), .in1(sumador_2_s), .in3(sumador_2_s), .in4(not_2_out), .in6(or_2_out), .out(R), .sel(Op));  // open: in2, in5, in7
endmodule

// A12
module ALU_bit_16 (
  input  [2:0] in_1,
  input  [15:0] in_2,
  input  [15:0] in_3,
  output [15:0] out_4,
  output out_5,
  output out_6
);

  wire alu_bit_1_1_cout, alu_bit_1_2_cout, alu_bit_1_3_cout, alu_bit_1_4_cout, alu_bit_1_5_cout,
       alu_bit_1_6_cout, alu_bit_1_7_cout, alu_bit_1_8_cout, alu_bit_1_9_cout, alu_bit_1_10_cout,
       alu_bit_1_11_cout, alu_bit_1_12_cout, alu_bit_1_13_cout, alu_bit_1_14_cout, alu_bit_1_15_cout;

  // Probe on in_2
  // Probe on in_3
  ALU_bit_1 alu_bit_1_1 (.R(out_4[0]), .A(in_2[0]), .B(in_3[0]), .Cint(1'b0), .Op(in_1), .Cout(alu_bit_1_1_cout));
  ALU_bit_1 alu_bit_1_2 (
    .R(out_4[1]), .A(in_2[1]), .B(in_3[1]), .Cint(alu_bit_1_1_cout), .Op(in_1), .Cout(alu_bit_1_2_cout));
  ALU_bit_1 alu_bit_1_3 (
    .R(out_4[2]), .A(in_2[2]), .B(in_3[2]), .Cint(alu_bit_1_2_cout), .Op(in_1), .Cout(alu_bit_1_3_cout));
  ALU_bit_1 alu_bit_1_4 (
    .R(out_4[3]), .A(in_2[3]), .B(in_3[3]), .Cint(alu_bit_1_3_cout), .Op(in_1), .Cout(alu_bit_1_4_cout));
  ALU_bit_1 alu_bit_1_5 (
    .R(out_4[4]), .A(in_2[4]), .B(in_3[4]), .Cint(alu_bit_1_4_cout), .Op(in_1), .Cout(alu_bit_1_5_cout));
  ALU_bit_1 alu_bit_1_6 (
    .R(out_4[5]), .A(in_2[5]), .B(in_3[5]), .Cint(alu_bit_1_5_cout), .Op(in_1), .Cout(alu_bit_1_6_cout));
  ALU_bit_1 alu_bit_1_7 (
    .R(out_4[6]), .A(in_2[6]), .B(in_3[6]), .Cint(alu_bit_1_6_cout), .Op(in_1), .Cout(alu_bit_1_7_cout));
  ALU_bit_1 alu_bit_1_8 (
    .R(out_4[7]), .A(in_2[7]), .B(in_3[7]), .Cint(alu_bit_1_7_cout), .Op(in_1), .Cout(alu_bit_1_8_cout));
  ALU_bit_1 alu_bit_1_9 (
    .R(out_4[8]), .A(in_2[8]), .B(in_3[8]), .Cint(alu_bit_1_8_cout), .Op(in_1), .Cout(alu_bit_1_9_cout));
  ALU_bit_1 alu_bit_1_10 (
    .R(out_4[9]), .A(in_2[9]), .B(in_3[9]), .Cint(alu_bit_1_9_cout), .Op(in_1), .Cout(alu_bit_1_10_cout));
  ALU_bit_1 alu_bit_1_11 (
    .R(out_4[10]), .A(in_2[10]), .B(in_3[10]), .Cint(alu_bit_1_10_cout), .Op(in_1), .Cout(alu_bit_1_11_cout));
  ALU_bit_1 alu_bit_1_12 (
    .R(out_4[11]), .A(in_2[11]), .B(in_3[11]), .Cint(alu_bit_1_11_cout), .Op(in_1), .Cout(alu_bit_1_12_cout));
  ALU_bit_1 alu_bit_1_13 (
    .R(out_4[12]), .A(in_2[12]), .B(in_3[12]), .Cint(alu_bit_1_12_cout), .Op(in_1), .Cout(alu_bit_1_13_cout));
  ALU_bit_1 alu_bit_1_14 (
    .R(out_4[13]), .A(in_2[13]), .B(in_3[13]), .Cint(alu_bit_1_13_cout), .Op(in_1), .Cout(alu_bit_1_14_cout));
  ALU_bit_1 alu_bit_1_15 (
    .R(out_4[14]), .A(in_2[14]), .B(in_3[14]), .Cint(alu_bit_1_14_cout), .Op(in_1), .Cout(alu_bit_1_15_cout));
  // Probe on alu_bit_1_15_cout
  ALU_BIT_1_overflow alu_bit_1_overflow_1 (
    .A(in_2[15]), .B(in_3[15]), .Cint(alu_bit_1_15_cout), .R(out_4[15]), .Cout(out_6), .Op(in_1),
    .overFlow(out_5));
  // Probe on out_4

  // Other names for the same wires on the sheet: A0 = in_2[0]; A1 = in_2[1]; A2 = in_2[2]; A3 = in_2[3]; A4 = in_2[4];
  //   A5 = in_2[5]; A6 = in_2[6]; A7 = in_2[7]; A8 = in_2[8]; A9 = in_2[9]; A10 = in_2[10]; A11 = in_2[11];
  //   A12 = in_2[12]; A13 = in_2[13]; A14 = in_2[14]; A15 = in_2[15]; B0 = in_3[0]; B1 = in_3[1]; B2 = in_3[2];
  //   B3 = in_3[3]; B4 = in_3[4]; B5 = in_3[5]; B6 = in_3[6]; B7 = in_3[7]; B8 = in_3[8]; B9 = in_3[9];
  //   B10 = in_3[10]; B11 = in_3[11]; B12 = in_3[12]; B13 = in_3[13]; B14 = in_3[14]; B15 = in_3[15]; OP[2:0] = in_1;
  //   R0 = out_4[0]; R1 = out_4[1]; R2 = out_4[2]; R3 = out_4[3]; R4 = out_4[4]; R5 = out_4[5]; R6 = out_4[6];
  //   R7 = out_4[7]; R8 = out_4[8]; R9 = out_4[9]; R10 = out_4[10]; R11 = out_4[11]; R12 = out_4[12]; R13 = out_4[13];
  //   R14 = out_4[14]; R15 = out_4[15]
endmodule

module ALU_BIT_1_overflow (
  input  A,
  input  B,
  input  Cint,
  input  [2:0] Op,
  output R,
  output overFlow,
  output Cout
);

  wire and_1_out, multiplexer_1_out, not_1_out, not_2_out, or_1_out, or_2_out, or_3_out, sumador_1_s,
       sumador_overflow_1_s;

  not not_1 (not_1_out, or_1_out);
  or or_1 (or_1_out, B, B);
  Sumador sumador_1 (.A(1'b1), .B(not_1_out), .Cin(1'b0), .S(sumador_1_s));  // open: Cout
  Multiplexer #(.select(3), .enable("false")) multiplexer_1 (
    .in0(B), .in1(sumador_1_s), .in2(B), .in3(B), .in4(B), .in5(B), .in6(B), .in7(B),
    .out(multiplexer_1_out), .sel(Op));
  and and_1 (and_1_out, B, A);
  or or_2 (or_2_out, B, A);
  not not_2 (not_2_out, or_3_out);
  or or_3 (or_3_out, B, A);
  Sumador_overflow sumador_overflow_1 (
    .A(multiplexer_1_out), .B(A), .Cin(Cint), .S(sumador_overflow_1_s), .Cout(Cout), .Overflow(overFlow));
  Multiplexer #(.select(3), .enable("false")) multiplexer_2 (
    .in0(and_1_out), .in1(sumador_overflow_1_s), .in3(sumador_overflow_1_s), .in4(not_2_out), .in6(or_2_out),
    .out(R), .sel(Op));  // open: in2, in5, in7
endmodule
