// Logisim project Lab2_computadores.circ as structural Verilog
module Reconocedor_sec (
);

  wire A, and_1_out, and_3_out, and_4_out, and_5_out, and_6_out, and_7_out, and_8_out, and_9_out, and_10_out,
       and_11_out, and_12_out, and_13_out, and_15_out, and_16_out, B, C, D, E, J2, J3, K2, K3, Y1, Y2, Y3, Y4;

  and and_1 (and_1_out, ~B, E);  // AND_Gate
  and and_2 (Y1, A, ~B, ~C, ~D);  // AND_Gate
  and and_3 (and_3_out, ~A, C);  // AND_Gate
  and and_4 (and_4_out, A, E);
  and and_5 (and_5_out, A, ~C, D);  // AND_Gate
  and and_6 (and_6_out, ~D, ~E);  // AND_Gate
  and and_7 (and_7_out, C, E);
  and and_8 (and_8_out, ~A, ~C, ~E);  // AND_Gate
  and and_9 (and_9_out, A, D, E);
  and and_10 (and_10_out, ~A, ~B, E);  // AND_Gate
  and and_11 (and_11_out, ~A, ~D, E);  // AND_Gate
  and and_12 (and_12_out, A, ~B, ~D);  // AND_Gate
  and and_13 (and_13_out, A, D, ~E);  // AND_Gate
  or or_1 (K3, ~D, A, and_1_out);  // OR_Gate
  or or_2 (J2, and_3_out, and_4_out, and_5_out);
  and and_14 (Y3, A, B, ~C, ~D);  // AND_Gate
  or or_3 (K2, and_6_out, and_7_out, and_8_out, and_9_out);
  or or_4 (J3, and_10_out, and_11_out, and_12_out, and_13_out);
  and and_15 (and_15_out, A, ~B, C, ~D);  // AND_Gate
  and and_16 (and_16_out, A, B, ~C, ~D);  // AND_Gate
  or or_5 (Y2, and_15_out, and_16_out);
  and and_17 (Y4, A, B, C, ~D);  // AND_Gate
endmodule
